// Digital circuit 8BitIR.dig as structural Verilog
module _8BitIR (
  input  Clk,
  input  [7:0] Input_Data,
  input  [1:0] CTR,
  output [7:0] Out
);

  CIS_310_1Byte_memory cis_310_1byte_memory_1 (.Input(Input_Data), .Clock(Clk), .Control(CTR), .\output (Out));

  // Notes on the sheet:
  //   Input_Data: Incrament
endmodule
