// Digital circuit ALU_Final.dig as structural Verilog
module ALU_Final (
  input  S1,
  input  S0,
  input  Cin,
  input  [7:0] A,
  input  [7:0] B,
  output [7:0] D
);

  wire [7:0] multiplexer_1_out, not_1_out;

  assign not_1_out = ~B;  // Not not_1, 8 bits wide
  Multiplexer #(.Selector_Bits(2), .Bits(8)) multiplexer_1 (
    .sel({S1, S0}), .in_0(B), .in_1(not_1_out), .in_2({8{1'b0}}), .in_3({8{1'b1}}), .out(multiplexer_1_out));
  Add #(.Bits(8)) add_1 (.a(A), .b(multiplexer_1_out), .c_i(Cin), .s(D));  // open: c_o
  // Probe on D
endmodule
