// Digital circuit CIS 310 1Byte memory.dig as structural Verilog
module CIS_310_1Byte_memory (
  input  [7:0] Input,
  input  Clock,
  input  [1:0] Control,
  output [7:0] \output 
);

  wire [7:0] multiplexer_1_out;

  Multiplexer #(.Selector_Bits(2), .Bits(8)) multiplexer_1 (
    .sel(Control), .in_0(\output ), .in_1(Input), .in_2({8{1'b0}}), .in_3({8{1'b1}}), .out(multiplexer_1_out));
  D_FF d_ff_1 (.D(multiplexer_1_out[7]), .C(Clock), .Q(\output [7]));  // open: nQ
  D_FF d_ff_2 (.D(multiplexer_1_out[6]), .C(Clock), .Q(\output [6]));  // open: nQ
  D_FF d_ff_3 (.D(multiplexer_1_out[5]), .C(Clock), .Q(\output [5]));  // open: nQ
  D_FF d_ff_4 (.D(multiplexer_1_out[4]), .C(Clock), .Q(\output [4]));  // open: nQ
  D_FF d_ff_5 (.D(multiplexer_1_out[3]), .C(Clock), .Q(\output [3]));  // open: nQ
  D_FF d_ff_6 (.D(multiplexer_1_out[2]), .C(Clock), .Q(\output [2]));  // open: nQ
  D_FF d_ff_7 (.D(multiplexer_1_out[1]), .C(Clock), .Q(\output [1]));  // open: nQ
  D_FF d_ff_8 (.D(multiplexer_1_out[0]), .C(Clock), .Q(\output [0]));  // open: nQ

  // Notes on the sheet:
  //   Control: 00 Load
  //   01 Store
  //   10 Clear
  //   11 ste FF
endmodule
