// Digital circuit CIS310_A2_ALU.dig as structural Verilog
module CIS310_A2_ALU (
  input  S1,
  input  S0,
  input  Cin,
  output [7:0] D
);

  wire [7:0] A0_out, B0_out, multiplexer_1_out, not_1_out;

  DipSwitch A0 (.out(A0_out[0]));
  DipSwitch A1 (.out(A0_out[1]));
  DipSwitch A2 (.out(A0_out[2]));
  DipSwitch A3 (.out(A0_out[3]));
  DipSwitch A4 (.out(A0_out[4]));
  DipSwitch A5 (.out(A0_out[5]));
  DipSwitch A6 (.out(A0_out[6]));
  DipSwitch A7 (.out(A0_out[7]));
  DipSwitch B0 (.out(B0_out[0]));
  DipSwitch B1 (.out(B0_out[1]));
  DipSwitch B2 (.out(B0_out[2]));
  DipSwitch B3 (.out(B0_out[3]));
  DipSwitch B4 (.out(B0_out[4]));
  DipSwitch B5 (.out(B0_out[5]));
  DipSwitch B6 (.out(B0_out[6]));
  DipSwitch B7 (.out(B0_out[7]));
  assign not_1_out = ~B0_out;  // Not not_1, 8 bits wide
  Multiplexer #(.Bits(8), .Selector_Bits(2)) multiplexer_1 (
    .sel({S1, S0}), .in_0(B0_out), .in_1(not_1_out), .in_2({8{1'b0}}), .in_3({8{1'b1}}),
    .out(multiplexer_1_out));
  Add #(.Bits(8)) add_1 (.a(A0_out), .b(multiplexer_1_out), .c_i(Cin), .s(D));  // open: c_o
  // Probe on D
endmodule
