// Digital circuit CIS350_A1_PC.dig as structural Verilog
module CIS350_A1_PC (
  input  INC,
  input  LD,
  input  RST,
  input  CLK,
  output [7:0] PC_OUT
);

  wire or_1_out, or_2_out;
  wire [7:0] add_1_s, DATA_IN_0_out, multiplexer_1_out, multiplexer_2_out;

  or or_1 (or_1_out, INC, LD);
  or or_2 (or_2_out, or_1_out, RST);
  DipSwitch DATA_IN_0 (.out(DATA_IN_0_out[0]));
  DipSwitch DATA_IN_1 (.out(DATA_IN_0_out[1]));
  DipSwitch DATA_IN_2 (.out(DATA_IN_0_out[2]));
  DipSwitch DATA_IN_3 (.out(DATA_IN_0_out[3]));
  DipSwitch DATA_IN_4 (.out(DATA_IN_0_out[4]));
  DipSwitch DATA_IN_5 (.out(DATA_IN_0_out[5]));
  DipSwitch DATA_IN_6 (.out(DATA_IN_0_out[6]));
  DipSwitch DATA_IN_7 (.out(DATA_IN_0_out[7]));
  Register #(.Bits(8)) PC (.D(multiplexer_2_out), .C(CLK), .en(or_2_out), .Q(PC_OUT));
  Add #(.Bits(8)) add_1 (.a(PC_OUT), .b(8'h1), .c_i(1'b0), .s(add_1_s));  // open: c_o
  Multiplexer #(.Bits(8)) multiplexer_1 (.sel(INC), .in_0(DATA_IN_0_out), .in_1(add_1_s), .out(multiplexer_1_out));
  Multiplexer #(.Bits(8)) multiplexer_2 (
    .sel(RST), .in_0(multiplexer_1_out), .in_1({8{1'b0}}), .out(multiplexer_2_out));
endmodule
