// Digital circuit Register File.dig as structural Verilog
module Register_File (
  input  Clk,
  input  [1:0] Read_Register1,
  input  [1:0] Read_Register2,
  input  [7:0] Write_Data,
  input  [1:0] Write_Register,
  input  WE,
  output [7:0] Read_Data1,
  output [7:0] Read_Data2
);

  wire and_1_out, and_2_out, and_3_out, and_4_out, decoder_1_out_0, decoder_1_out_1, decoder_1_out_2,
       decoder_1_out_3;
  wire [7:0] R_0_q, R_1_q, R_2_q, R_3_q;

  Decoder #(.Selector_Bits(2)) decoder_1 (
    .sel(Write_Register), .out_0(decoder_1_out_0), .out_1(decoder_1_out_1), .out_2(decoder_1_out_2),
    .out_3(decoder_1_out_3));
  and and_1 (and_1_out, WE, decoder_1_out_0);
  and and_2 (and_2_out, WE, decoder_1_out_1);
  and and_3 (and_3_out, WE, decoder_1_out_2);
  and and_4 (and_4_out, WE, decoder_1_out_3);
  Register #(.Bits(8)) R_0 (.D(Write_Data), .C(Clk), .en(and_1_out), .Q(R_0_q));
  Register #(.Bits(8)) R_1 (.D(Write_Data), .C(Clk), .en(and_2_out), .Q(R_1_q));
  Register #(.Bits(8)) R_2 (.D(Write_Data), .C(Clk), .en(and_3_out), .Q(R_2_q));
  Register #(.Bits(8)) R_3 (.D(Write_Data), .C(Clk), .en(and_4_out), .Q(R_3_q));
  Multiplexer #(.Bits(8), .Selector_Bits(2)) multiplexer_1 (
    .sel(Read_Register1), .in_0(R_0_q), .in_1(R_1_q), .in_2(R_2_q), .in_3(R_3_q), .out(Read_Data1));
  Multiplexer #(.Bits(8), .Selector_Bits(2)) multiplexer_2 (
    .sel(Read_Register2), .in_0(R_0_q), .in_1(R_1_q), .in_2(R_2_q), .in_3(R_3_q), .out(Read_Data2));
endmodule
