// Digital circuit RegisterFile.dig as structural Verilog
module RegisterFile (
  input  [7:0] CTRL,
  input  [7:0] Write_Data,
  input  Clk,
  input  [1:0] Write_Register,
  input  [1:0] Read_Register2,
  input  [1:0] Read_Register1,
  output [7:0] Read_Data_1,
  output [7:0] Read_Data_2
);

  wire [7:0] demultiplexer_1_out_0, demultiplexer_1_out_1, demultiplexer_1_out_2, demultiplexer_1_out_3,
       R_0_output, R_1_output, R_2_output, R_3_output;

  Demultiplexer #(.Selector_Bits(2), .Bits(8)) demultiplexer_1 (
    .sel(Write_Register), .in(Write_Data), .out_0(demultiplexer_1_out_0), .out_1(demultiplexer_1_out_1),
    .out_2(demultiplexer_1_out_2), .out_3(demultiplexer_1_out_3));
  CIS_310_1Byte_memory R_0 (.Input(demultiplexer_1_out_0), .Clock(Clk), .Control(CTRL[1:0]), .\output (R_0_output));
  CIS_310_1Byte_memory R_1 (.Input(demultiplexer_1_out_1), .Clock(Clk), .Control(CTRL[3:2]), .\output (R_1_output));
  CIS_310_1Byte_memory R_2 (.Input(demultiplexer_1_out_2), .Clock(Clk), .Control(CTRL[5:4]), .\output (R_2_output));
  CIS_310_1Byte_memory R_3 (.Input(demultiplexer_1_out_3), .Clock(Clk), .Control(CTRL[7:6]), .\output (R_3_output));
  Multiplexer #(.Selector_Bits(2), .Bits(8)) multiplexer_1 (
    .sel(Read_Register1), .in_0(R_0_output), .in_1(R_1_output), .in_2(R_2_output), .in_3(R_3_output),
    .out(Read_Data_1));
  Multiplexer #(.Selector_Bits(2), .Bits(8)) multiplexer_2 (
    .sel(Read_Register2), .in_0(R_0_output), .in_1(R_1_output), .in_2(R_2_output), .in_3(R_3_output),
    .out(Read_Data_2));
endmodule
